// Logisim project Circuito Final.circ as structural Verilog: 3 circuits, main circuit Display
module Display (
  input  M2,
  input  M1,
  output a,
  output b,
  output c,
  output d,
  output e,
  output f,
  output g
);

  wire not_1_out, not_2_out, not_3_out, not_5_out, not_6_out;

  not not_1 (not_1_out, M1);
  not not_2 (not_2_out, M2);
  not not_3 (not_3_out, M1);
  not not_4 (e, M1);
  not not_5 (not_5_out, M2);
  not not_6 (not_6_out, M1);
  or or_1 (a, not_1_out, M2);
  or or_2 (c, not_2_out, M1);
  or or_3 (d, not_3_out, M2);
  and and_1 (f, not_5_out, not_6_out);

  assign b = 1'b1;
  assign g = M2;
endmodule

module \Servir_o_café  (
  input  BI,
  output LCP
);

  wire and_1_out, and_2_out, and_3_out, and_4_out, and_5_out, clock_1_out, D0_q, D0_qn, D1_q, D1_qn, D2_q,
       D2_qn, or_1_out, or_2_out;

  Clock clock_1 (.out(clock_1_out));
  LED led_1 (.in(BI));
  and and_1 (and_1_out, BI, D0_qn);
  D_Flip_Flop D2 (.clk(clock_1_out), .D(or_1_out), .Q(D2_q), .Qn(D2_qn));  // open: preset, en, reset
  D_Flip_Flop D1 (.clk(clock_1_out), .D(or_2_out), .Q(D1_q), .Qn(D1_qn));  // open: preset, en, reset
  D_Flip_Flop D0 (.clk(clock_1_out), .D(and_1_out), .Q(D0_q), .Qn(D0_qn));  // open: preset, en, reset
  and and_2 (and_2_out, D2_qn, D0_q, D1_qn);
  and and_3 (and_3_out, D1_q, D0_q);
  and and_4 (and_4_out, D2_q, D0_qn);
  and and_5 (and_5_out, D1_q, D0_qn);
  and and_6 (LCP, D2_q, D0_q);
  or or_1 (or_1_out, and_4_out, and_3_out);
  or or_2 (or_2_out, and_5_out, and_2_out);
endmodule

module Circuito_Final_2 (
);

  wire and_1_out, and_2_out, and_3_out, and_4_out, and_5_out, and_6_out, and_7_out, and_8_out, BI_out,
       clock_1_out, D0_q, D0_qn, D1_q, D1_qn, display_1_a, display_1_b, display_1_c, display_1_d,
       display_1_e, display_1_f, display_1_g, M1_out, M2_out, nand_1_out, not_1_out, or_1_out, or_2_out,
       \servir_o_café_1_lcp ;

  Clock clock_1 (.out(clock_1_out));
  Button M2 (.out(M2_out));
  Button M1 (.out(M1_out));
  Button BI (.out(BI_out));
  not not_1 (not_1_out, M1_out);
  and and_1 (and_1_out, M2_out, not_1_out, D1_qn);
  and and_2 (and_2_out, D1_q, D0_qn);
  and and_3 (and_3_out, D1_qn, M1_out, D0_q);
  and and_4 (and_4_out, BI_out, and_8_out);
  \Servir_o_café  \servir_o_café_1  (.BI(and_4_out), .LCP(\servir_o_café_1_lcp ));
  or or_1 (or_1_out, and_1_out, and_2_out, and_3_out);
  LED LCP (.in(\servir_o_café_1_lcp ));
  D_Flip_Flop D1 (
    .clk(clock_1_out), .D(or_1_out), .Q(D1_q), .Qn(D1_qn), .en(nand_1_out), .reset(\servir_o_café_1_lcp ));  // open: preset
  D_Flip_Flop D0 (
    .clk(clock_1_out), .D(or_2_out), .Q(D0_q), .Qn(D0_qn), .en(nand_1_out), .reset(\servir_o_café_1_lcp ));  // open: preset
  and and_5 (and_5_out, M2_out, D0_qn, D1_q);
  and and_6 (and_6_out, D0_q, D1_qn, not_1_out);
  and and_7 (and_7_out, D0_qn, M1_out);
  Display display_1 (
    .M2(D1_q), .M1(D0_q), .a(display_1_a), .b(display_1_b), .c(display_1_c), .d(display_1_d),
    .e(display_1_e), .f(display_1_f), .g(display_1_g));
  or or_2 (or_2_out, and_6_out, and_7_out, and_5_out);
  _7_Segment_Display u_7_segment_display_1 (
    .g(display_1_g), .f(display_1_f), .a(display_1_a), .b(display_1_b), .e(display_1_e), .d(display_1_d),
    .c(display_1_c));  // open: dp
  LED led_1 (.in(and_8_out));
  and and_8 (and_8_out, D1_q, D0_q);
  nand nand_1 (nand_1_out, display_1_g, display_1_b, display_1_a, display_1_c, display_1_d);

  // Notes on the sheet:
  //   MOEDEIRO DE 0,20 €
  //   MOEDEIRO DE 0,10 €
  //   Botão para fazer café
  //   Módulo Servir o Café
  //   Lâmpada café pronto
  //   Dinheiro Suficiente
endmodule
