// Logisim project Moedeiro.circ as structural Verilog: 2 circuits, main circuit main
module main (
  input  in_1,
  input  in_2
);

  wire and_1_out, and_2_out, and_3_out, and_4_out, and_5_out, and_6_out, and_7_out, clock_1_out, D0_q, D0_qn,
       D1_q, D1_qn, display_1_a, display_1_b, display_1_c, display_1_d, display_1_e, display_1_f,
       display_1_g, M1_out, M2_out, nand_1_out, not_1_out, or_1_out, or_2_out;

  Clock clock_1 (.out(clock_1_out));
  Button M2 (.out(M2_out));
  Button M1 (.out(M1_out));
  not not_1 (not_1_out, M1_out);
  and and_1 (and_1_out, M2_out, not_1_out, D1_qn);
  and and_2 (and_2_out, D1_q, D0_qn);
  and and_3 (and_3_out, D1_qn, M1_out, D0_q);
  D_Flip_Flop D1 (
    .clk(clock_1_out), .D(or_1_out), .Q(D1_q), .Qn(D1_qn), .en(nand_1_out), .reset(in_1));  // open: preset
  or or_1 (or_1_out, and_1_out, and_2_out, and_3_out);
  D_Flip_Flop D0 (
    .clk(clock_1_out), .D(or_2_out), .Q(D0_q), .Qn(D0_qn), .en(nand_1_out), .reset(in_2));  // open: preset
  and and_4 (and_4_out, M2_out, D0_qn, D1_q);
  and and_5 (and_5_out, D0_q, D1_qn, not_1_out);
  and and_6 (and_6_out, D0_qn, M1_out);
  Display display_1 (
    .M2(D1_q), .M1(D0_q), .a(display_1_a), .b(display_1_b), .c(display_1_c), .d(display_1_d),
    .e(display_1_e), .f(display_1_f), .g(display_1_g));
  or or_2 (or_2_out, and_5_out, and_6_out, and_4_out);
  _7_Segment_Display u_7_segment_display_1 (
    .g(display_1_g), .f(display_1_f), .a(display_1_a), .b(display_1_b), .e(display_1_e), .d(display_1_d),
    .c(display_1_c));  // open: dp
  LED led_1 (.in(and_7_out));
  and and_7 (and_7_out, D1_q, D0_q);
  nand nand_1 (nand_1_out, display_1_g, display_1_b, display_1_a, display_1_c, display_1_d);
endmodule

module Display (
  input  M2,
  input  M1,
  output a,
  output b,
  output c,
  output d,
  output e,
  output f,
  output g
);

  wire not_1_out, not_2_out, not_3_out, not_5_out, not_6_out;

  not not_1 (not_1_out, M1);
  not not_2 (not_2_out, M2);
  not not_3 (not_3_out, M1);
  not not_4 (e, M1);
  not not_5 (not_5_out, M2);
  not not_6 (not_6_out, M1);
  or or_1 (a, not_1_out, M2);
  or or_2 (c, not_2_out, M1);
  or or_3 (d, not_3_out, M2);
  and and_1 (f, not_5_out, not_6_out);

  assign b = 1'b1;
  assign g = M2;
endmodule
